// Logisim project Module_5_NormUnit.circ as structural Verilog: 4 circuits, main circuit NormUnit
module NormUnit (
  input  [14:0] Raw_Sum,
  input  [4:0] Exp_In,
  input  Sign_In,
  output Is_Zero,
  output [4:0] Exp_Out,
  output [10:0] Norm_Mantissa,
  output G_Out,
  output R_Out,
  output S_Out,
  output Sign_Out
);

  wire [3:0] clz_14bit_1_shift_amt;

  CLZ_14bit clz_14bit_1 (.Data_In(Raw_Sum[13:0]), .Is_Zero(Is_Zero), .Shift_Amt(clz_14bit_1_shift_amt));
  Exp_Adjuster exp_adjuster_1 (
    .Exp_In(Exp_In), .Shift_Amt(clz_14bit_1_shift_amt), .Right_Shift(Raw_Sum[14]), .Exp_Out(Exp_Out));
  Norm_Shifter norm_shifter_1 (
    .Raw_Sum(Raw_Sum), .Shift_Amt(clz_14bit_1_shift_amt), .Norm_Data({Norm_Mantissa, G_Out, R_Out, S_Out}));

  assign Sign_Out = Sign_In;
endmodule

module CLZ_14bit (
  input  [13:0] Data_In,
  output Is_Zero,
  output [3:0] Shift_Amt
);

  wire priority_encoder_1_gs, subtractor_1_bout;
  wire [3:0] priority_encoder_1_out, subtractor_1_out;

  Priority_Encoder #(.select(4)) priority_encoder_1 (
    .in0(Data_In[0]), .in1(Data_In[1]), .in2(Data_In[2]), .in3(Data_In[3]), .in4(Data_In[4]),
    .in5(Data_In[5]), .in6(Data_In[6]), .in7(Data_In[7]), .in8(Data_In[8]), .in9(Data_In[9]),
    .in10(Data_In[10]), .in11(Data_In[11]), .in12(Data_In[12]), .in13(Data_In[13]), .in14(1'b0), .in15(1'b0),
    .out(priority_encoder_1_out), .gs(priority_encoder_1_gs), .en_in(1'b1));  // open: en_out
  Subtractor #(.width(4)) subtractor_1 (
    .a(4'b1101), .b(priority_encoder_1_out), .out(subtractor_1_out), .bin(1'b0), .bout(subtractor_1_bout));
  not not_1 (Is_Zero, priority_encoder_1_gs);
  Multiplexer #(.width(4)) multiplexer_1 (.in0(subtractor_1_out), .in1(4'b0000), .out(Shift_Amt), .sel(Is_Zero));
endmodule

module Exp_Adjuster (
  input  [4:0] Exp_In,
  input  [3:0] Shift_Amt,
  input  Right_Shift,
  output [4:0] Exp_Out
);

  wire [4:0] adder_1_out, bit_extender_1_out, subtractor_1_out;

  assign bit_extender_1_out = {{1{1'b0}}, Shift_Amt};  // Bit_Extender bit_extender_1
  Adder #(.width(5)) adder_1 (.a(Exp_In), .b(5'b00001), .out(adder_1_out), .cin(1'b0));  // open: cout
  Subtractor #(.width(5)) subtractor_1 (
    .a(Exp_In), .b(bit_extender_1_out), .out(subtractor_1_out), .bin(1'b0));  // open: bout
  Multiplexer #(.width(5)) multiplexer_1 (.in0(subtractor_1_out), .in1(adder_1_out), .out(Exp_Out), .sel(Right_Shift));
endmodule

module Norm_Shifter (
  input  [14:0] Raw_Sum,
  input  [3:0] Shift_Amt,
  output [13:0] Norm_Data
);

  wire [0:0] or_1_out;
  wire [13:0] shifter_1_out;

  or or_1 (or_1_out[0], Raw_Sum[1], Raw_Sum[0]);
  Shifter #(.width(14)) shifter_1 (.in(Raw_Sum[13:0]), .\dist (Shift_Amt), .out(shifter_1_out));
  Multiplexer #(.width(14)) multiplexer_1 (
    .in0(shifter_1_out), .in1({Raw_Sum[14:2], or_1_out[0]}), .out(Norm_Data), .sel(Raw_Sum[14]));
endmodule
